// Logisim project 1bitAdder.circ as structural Verilog: 2 circuits, main circuit main
module main (
  input  A,
  input  B,
  input  P,
  output S,
  output P_2
);

  wire not_1_out, not_2_out, not_3_out, or_1_out, or_2_out, or_3_out, or_4_out, or_5_out, or_6_out, or_7_out;

  not not_1 (not_1_out, A);
  not not_2 (not_2_out, B);
  not not_3 (not_3_out, P);
  or or_1 (or_1_out, A, not_2_out, not_3_out);
  or or_2 (or_2_out, not_1_out, B, not_3_out);
  or or_3 (or_3_out, not_1_out, not_2_out, P);
  or or_4 (or_4_out, A, B, P);
  and and_1 (S, or_1_out, or_2_out, or_3_out, or_4_out);
  or or_5 (or_5_out, A, P);
  or or_6 (or_6_out, A, B);
  or or_7 (or_7_out, B, P);
  and and_2 (P_2, or_5_out, or_6_out, or_7_out);

  // Notes on the sheet:
  //   A
  //   P
  //   B
  //   !B
  //   !A
  //   !P
endmodule

module main_f (
  input  [7:0] in_1,
  input  [7:0] in_2,
  output [7:0] out_3
);

  wire main_1_s, main_2_s, main_3_s, main_4_s, main_5_s, main_6_s, main_7_s, main_8_s;

  // Probe on in_1
  // Probe on in_2
  main main_1 (.A(in_1[0]), .B(in_2[0]), .P(main_8_s), .S(main_1_s), .P_2(out_3[0]));
  main main_2 (.A(in_1[1]), .B(in_2[1]), .P(main_1_s), .S(main_2_s), .P_2(out_3[1]));
  main main_3 (.A(in_1[2]), .B(in_2[2]), .P(main_2_s), .S(main_3_s), .P_2(out_3[2]));
  main main_4 (.A(in_1[3]), .B(in_2[3]), .P(main_3_s), .S(main_4_s), .P_2(out_3[3]));
  main main_5 (.A(in_1[4]), .B(in_2[4]), .P(main_4_s), .S(main_5_s), .P_2(out_3[4]));
  main main_6 (.A(in_1[5]), .B(in_2[5]), .P(main_5_s), .S(main_6_s), .P_2(out_3[5]));
  main main_7 (.A(in_1[6]), .B(in_2[6]), .P(main_6_s), .S(main_7_s), .P_2(out_3[6]));
  main main_8 (.A(in_1[7]), .B(in_2[7]), .P(main_7_s), .S(main_8_s), .P_2(out_3[7]));
  // Probe on out_3
endmodule
