// Logisim project BCD8421_BCD8421_9_4bit.circ as structural Verilog: 2 circuits, main circuit main
module main (
  input  [3:0] BCD8421,
  output [3:0] BCD8421_9,
  output Y3,
  output Y2,
  output Y1,
  output Y0
);

  wire and_1_out, and_2_out, and_3_out, and_4_out, and_5_out, and_6_out, and_7_out, and_8_out, and_9_out,
       and_10_out, and_11_out, not_1_out, not_2_out, not_3_out, not_4_out;

  // Probe on BCD8421
  not not_1 (not_1_out, BCD8421[3]);
  not not_2 (not_2_out, BCD8421[2]);
  not not_3 (not_3_out, BCD8421[1]);
  not not_4 (not_4_out, BCD8421[0]);
  and and_1 (and_1_out, not_1_out, not_4_out);
  and and_2 (and_2_out, not_2_out, not_4_out, not_3_out);
  and and_3 (and_3_out, not_1_out, not_3_out, BCD8421[0]);
  and and_4 (and_4_out, not_1_out, not_4_out, BCD8421[1]);
  and and_5 (and_5_out, not_2_out, BCD8421[0], not_3_out);
  and and_6 (and_6_out, not_1_out, not_2_out, BCD8421[1], BCD8421[0]);
  and and_7 (and_7_out, not_1_out, BCD8421[2], not_3_out);
  and and_8 (and_8_out, not_1_out, BCD8421[2], not_4_out);
  and and_9 (and_9_out, not_1_out, not_2_out);
  and and_10 (and_10_out, not_1_out, not_3_out);
  and and_11 (and_11_out, not_1_out, not_4_out);
  or or_1 (BCD8421_9[0], and_1_out, and_2_out);
  or or_2 (BCD8421_9[1], and_3_out, and_4_out, and_5_out);
  or or_3 (BCD8421_9[2], and_6_out, and_7_out, and_8_out);
  or or_4 (BCD8421_9[3], and_9_out, and_10_out, and_11_out);
  // Probe on BCD8421_9

  assign Y0 = BCD8421_9[3];
  assign Y1 = BCD8421_9[2];
  assign Y2 = BCD8421_9[1];
  assign Y3 = BCD8421_9[0];

  // Notes on the sheet:
  //   B
  //   C
  //   A
  //   !C
  //   !B
  //   !A
  //   D
  //   !D
endmodule

module main_f (
  input  [7:0] in_1,
  input  [7:0] in_2,
  output [7:0] out_3
);

  wire main_1_p3, main_1_p6, main_2_p6, main_3_p6, main_4_p6, main_5_p6, main_6_p6, main_7_p6;

  // Probe on in_1
  // Probe on in_2
  // main main_1: pin names not known; wires that end beside it: in_1[0], in_2[0], main_1_p3, in_1[1], in_2[1], main_1_p6, out_3[0], main_1_p3
  // main main_2: pin names not known; wires that end beside it: in_1[1], in_2[1], main_1_p6, in_1[2], in_2[2], main_2_p6, out_3[1], main_1_p6
  // main main_3: pin names not known; wires that end beside it: in_1[2], in_2[2], main_2_p6, in_1[3], in_2[3], main_3_p6, out_3[2], main_2_p6
  // main main_4: pin names not known; wires that end beside it: in_1[3], in_2[3], main_3_p6, in_1[4], in_2[4], main_4_p6, out_3[3], main_3_p6
  // main main_5: pin names not known; wires that end beside it: in_1[4], in_2[4], main_4_p6, in_1[5], in_2[5], main_5_p6, out_3[4], main_4_p6
  // main main_6: pin names not known; wires that end beside it: in_1[5], in_2[5], main_5_p6, in_1[6], in_2[6], main_6_p6, out_3[5], main_5_p6
  // main main_7: pin names not known; wires that end beside it: in_1[6], in_2[6], main_6_p6, in_1[7], in_2[7], main_7_p6, out_3[6], main_6_p6
  // main main_8: pin names not known; wires that end beside it: in_1[7], in_2[7], main_7_p6, main_1_p3, out_3[7], main_7_p6
  // Probe on out_3
endmodule
