// Logisim project 4bitSubstractor.circ as structural Verilog: 1 circuit, main circuit main
module main (
  input  V,
  input  V_2,
  input  V_3,
  input  V_4,
  input  V_5,
  input  V_6
);

  wire and_1_out, and_2_out, and_3_out, clock_1_out, D_q, JK_q, nq1_out, nq2_out, nq3_out, RS_q;
  wire [3:0] T1_q;

  Clock clock_1 (.out(clock_1_out));
  not nq3 (nq3_out, T1_q[2]);
  not nq2 (nq2_out, T1_q[1]);
  not nq1 (nq1_out, T1_q[0]);
  D_Flip_Flop D (.clk(clock_1_out), .D(V_2), .Q(D_q));  // open: Qn, preset, en, reset
  S_R_Flip_Flop RS (.S(V_3), .clk(clock_1_out), .R(V_4), .Q(RS_q));  // open: Qn, preset, reset, en
  J_K_Flip_Flop JK (.J(V_5), .clk(clock_1_out), .K(V_6), .Q(JK_q));  // open: Qn, preset, en, reset
  and and_1 (and_1_out, nq3_out, nq1_out, nq2_out, V);
  and and_2 (and_2_out, nq2_out, nq1_out, V);
  and and_3 (and_3_out, nq1_out, V);
  T_Flip_Flop T4 (.clk(clock_1_out), .T(and_1_out), .Q(T1_q[3]));  // open: Qn, preset, reset, en
  T_Flip_Flop T3 (.clk(clock_1_out), .T(and_2_out), .Q(T1_q[2]));  // open: Qn, preset, reset, en
  T_Flip_Flop T2 (.clk(clock_1_out), .T(and_3_out), .Q(T1_q[1]));  // open: Qn, preset, reset, en
  T_Flip_Flop T1 (.clk(clock_1_out), .T(V), .Q(T1_q[0]));  // open: Qn, preset, reset, en
  // Probe on T1_q

  // Notes on the sheet:
  //   q4
  //   q3
  //   q2
  //   q1
  //   v
endmodule
